# Fritzing sketch pcb_pump_module (saved by Fritzing 0.9.3b)
perfboards: 1

parts:
  R1 = Resistor [tolerance=±5% resistance=220 package=THT]
  R2 = Resistor [tolerance=±5% resistance=220 package=THT]  # not connected
  R3 = Resistor [tolerance=±5% resistance=220 package=THT]  # not connected
  R4 = Resistor [tolerance=±5% resistance=220 package=THT]  # not connected
  Q1 = NPN-Transistor [package="TO92 [THT]"]
  C1 = Electrolytic Capacitor [capacitance=1µF package="100 mil [THT, electrolytic]"]  # not connected

nets:
  N1: R1.Pin_0, Q1.C
